# Fritzing sketch MotorBoard (saved by Fritzing 0.9.3b)
circuit board: 5.965cm x 6.99999cm
breadboards: 1

parts:
  Arduino_Mini_Pro = Arduino Pro Mini v13
  DR_B-EN = female pin header, 8 pins [form="♀ (female)"]
  part = female pin header, 8 pins [form="♀ (female)"]
  part_2 = female pin header, 8 pins [form="♀ (female)"]
  DR_A-EN = female pin header, 8 pins [form="♀ (female)"]
  GND/12V = Screw terminal - 2 pins [package=THT]
  D1 = Rectifier Diode [part_number=1N4001 package="300 mil [THT]"]
  DR_B_AA'BB' = screw terminal, 4 pins
  DR_A_AA'BB' = screw terminal, 4 pins
  part_3 = screw terminal, 4 pins
  GND/5V = Screw terminal - 2 pins [package=THT]
  D2 = Rectifier Diode [part_number=1N4001 package="300 mil [THT]"]
  C1 = Electrolytic Capacitor [capacitance=0.1mF voltage=20V package="200 mil [THT, electrolytic]"]

nets:
  N1: Arduino_Mini_Pro.RAW, DR_B-EN.pin7, part_2.pin7, D1.cathode
  N2: Arduino_Mini_Pro.GND, DR_B-EN.pin8, part_2.pin8, GND/5V.pin1
  N3: Arduino_Mini_Pro.A1, part.pin1
  N4: Arduino_Mini_Pro.A0, DR_A-EN.pin1
  N5: Arduino_Mini_Pro.D13/SCK, part_3.pin2
  N6: Arduino_Mini_Pro.D12/MISO, part_3.pin3
  N7: Arduino_Mini_Pro.D11_PWM/MOSI, part_3.pin4
  N8: Arduino_Mini_Pro.D10_PWM/SS, part_3.pin1
  N9: Arduino_Mini_Pro.D8, part.pin2, DR_A-EN.pin2
  N10: Arduino_Mini_Pro.D7, part.pin3, DR_A-EN.pin3
  N11: Arduino_Mini_Pro.D6_PWM, part.pin4, DR_A-EN.pin4
  N12: Arduino_Mini_Pro.D5_PWM, part.pin7
  N13: Arduino_Mini_Pro.D4, part.pin8
  N14: Arduino_Mini_Pro.D3_PWM, DR_A-EN.pin7
  N15: Arduino_Mini_Pro.D2, DR_A-EN.pin8
  N16: DR_B-EN.pin1, part_2.pin1, D2.cathode, C1.+
  N17: DR_B-EN.pin2, part_2.pin2, GND/12V.pin1, C1.-
  N18: DR_B-EN.pin3, DR_B_AA'BB'.pin4
  N19: DR_B-EN.pin4, DR_B_AA'BB'.pin3
  N20: DR_B-EN.pin5, DR_B_AA'BB'.pin2
  N21: DR_B-EN.pin6, DR_B_AA'BB'.pin1
  N22: part.pin5, part.pin6
  N23: part_2.pin3, DR_A_AA'BB'.pin1
  N24: part_2.pin4, DR_A_AA'BB'.pin2
  N25: part_2.pin5, DR_A_AA'BB'.pin3
  N26: part_2.pin6, DR_A_AA'BB'.pin4
  N27: DR_A-EN.pin5, DR_A-EN.pin6
  N28: GND/12V.pin2, D2.anode
  N29: D1.anode, GND/5V.pin2

notes:
  SS/SCK/MISO/MOSI
  TSC
  Focusdrive
  W. Birkfellner
  2017-V1.1
